// Logisim project semaforo.circ as structural Verilog: 7 circuits, main circuit main
module main (
);

  wire and_1_out, and_2_out, and_3_out, and_4_out, and_5_out, and_6_out, and_7_out, and_8_out, and_9_out,
       clock_1_out, counter_1_carry, counter_2_carry, counter_3_carry, counter_4_carry, counter_5_carry,
       not_1_out, not_2_out, not_3_out, not_4_out, not_5_out, not_6_out, not_7_out, not_8_out, not_9_out,
       not_10_out, or_1_out;

  not not_1 (not_1_out, counter_5_carry);
  not not_2 (not_2_out, or_1_out);
  and and_1 (and_1_out, not_9_out, counter_5_carry);
  and and_2 (and_2_out, not_10_out, counter_5_carry);
  Clock clock_1 (.out(clock_1_out));
  and and_3 (and_3_out, not_3_out, counter_1_carry);
  Counter #(.max('h6), .trigger("falling")) counter_1 (
    .count(and_2_out), .carry(counter_1_carry), .clk(clock_1_out));  // open: load, D, Q, clr
  not not_3 (not_3_out, and_5_out);
  Counter #(.max('h2), .trigger("falling")) counter_2 (
    .count(and_3_out), .carry(counter_2_carry), .clk(clock_1_out));  // open: load, D, Q, clr
  not not_4 (not_4_out, counter_1_carry);
  and and_4 (and_4_out, counter_5_carry, counter_4_carry);
  Counter #(.max('h4)) counter_3 (
    .count(and_4_out), .carry(counter_3_carry), .clk(clock_1_out));  // open: load, D, Q, clr
  Counter #(.max('h2)) counter_4 (
    .count(and_1_out), .carry(counter_4_carry), .clk(clock_1_out));  // open: load, D, Q, clr
  Counter #(.max('h10)) counter_5 (
    .count(not_2_out), .carry(counter_5_carry), .clk(clock_1_out));  // open: load, D, Q, clr
  and and_5 (and_5_out, not_1_out, not_10_out, not_10_out);
  not not_5 (not_5_out, counter_2_carry);
  and and_6 (and_6_out, not_4_out, counter_5_carry);
  not not_6 (not_6_out, counter_3_carry);
  not not_7 (not_7_out, counter_4_carry);
  not not_8 (not_8_out, counter_5_carry);
  and and_7 (and_7_out, not_5_out, counter_1_carry);
  not not_9 (not_9_out, and_8_out);
  and and_8 (and_8_out, not_6_out, counter_4_carry);
  and and_9 (and_9_out, counter_5_carry, not_7_out);
  not not_10 (not_10_out, and_7_out);
  or or_1 (or_1_out, and_8_out, and_9_out);
  LED led_1 (.in(and_5_out));
  LED led_2 (.in(and_7_out));
  LED led_3 (.in(and_6_out));
  LED led_4 (.in(and_8_out));
  LED led_5 (.in(and_9_out));
  LED led_6 (.in(not_8_out));

  // Notes on the sheet:
  //   Via V
  //   Via H
endmodule

module _6 (
  output [3:0] Saida_Segundo
);

  wire clock_1_out;

  Clock clock_1 (.out(clock_1_out));
  Counter #(.width(4), .max('h6)) counter_1 (.Q(Saida_Segundo), .clk(clock_1_out));  // open: load, D, count, carry, clr
endmodule

module _16 (
  input  in_1,
  output [3:0] out_2,
  output [3:0] out_3
);

  wire counter_1_carry, counter_2_carry, d_ff_1_q, d_ff_2_q, d_ff_3_q, d_ff_4_q, d_ff_5_q, d_ff_6_q, d_ff_7_q;

  Counter #(.width(4), .max('h1), .ongoal("load"), .trigger("falling")) counter_1 (
    .Q(out_2), .carry(counter_1_carry), .clk(counter_2_carry), .clr(d_ff_7_q));  // open: load, D, count
  D_Flip_Flop d_ff_1 (.clk(in_1), .D(counter_1_carry), .Q(d_ff_1_q), .reset(d_ff_7_q));  // open: Qn, preset, en
  D_Flip_Flop d_ff_2 (.clk(in_1), .D(d_ff_1_q), .Q(d_ff_2_q), .reset(d_ff_7_q));  // open: Qn, preset, en
  D_Flip_Flop d_ff_3 (.clk(in_1), .D(d_ff_2_q), .Q(d_ff_3_q), .reset(d_ff_7_q));  // open: Qn, preset, en
  D_Flip_Flop d_ff_4 (.clk(in_1), .D(d_ff_3_q), .Q(d_ff_4_q), .reset(d_ff_7_q));  // open: Qn, preset, en
  D_Flip_Flop d_ff_5 (.clk(in_1), .D(d_ff_4_q), .Q(d_ff_5_q), .reset(d_ff_7_q));  // open: Qn, preset, en
  Counter #(.width(4), .max('h9), .ongoal("load")) counter_2 (
    .Q(out_3), .carry(counter_2_carry), .clk(in_1), .clr(d_ff_7_q));  // open: load, D, count
  D_Flip_Flop d_ff_6 (.clk(in_1), .D(d_ff_5_q), .Q(d_ff_6_q), .reset(d_ff_7_q));  // open: Qn, preset, en
  D_Flip_Flop d_ff_7 (.clk(in_1), .D(d_ff_6_q), .Q(d_ff_7_q), .reset(d_ff_7_q));  // open: Qn, preset, en
endmodule

module _4 (
  output [3:0] Saida_Segundo
);

  wire clock_1_out;

  Clock clock_1 (.out(clock_1_out));
  Counter #(.width(4), .max('h4)) counter_1 (.Q(Saida_Segundo), .clk(clock_1_out));  // open: load, D, count, carry, clr
endmodule

module _2 (
  output [3:0] Saida_Segundo
);

  wire clock_1_out;

  Clock clock_1 (.out(clock_1_out));
  Counter #(.width(4), .max('h2)) counter_1 (.Q(Saida_Segundo), .clk(clock_1_out));  // open: load, D, count, carry, clr
endmodule

module _12 (
  output [3:0] out_1,
  output [3:0] out_2
);

  wire clock_1_out, counter_1_carry, counter_2_carry, d_ff_1_q, d_ff_2_q, d_ff_3_q;

  Clock clock_1 (.out(clock_1_out));
  Counter #(.width(4), .max('h1), .trigger("falling")) counter_1 (
    .Q(out_1), .carry(counter_1_carry), .clk(counter_2_carry), .clr(d_ff_3_q));  // open: load, D, count
  D_Flip_Flop d_ff_1 (.clk(clock_1_out), .D(counter_1_carry), .Q(d_ff_1_q), .reset(d_ff_3_q));  // open: Qn, preset, en
  Counter #(.width(4), .max('h9)) counter_2 (
    .Q(out_2), .carry(counter_2_carry), .clk(clock_1_out), .clr(d_ff_3_q));  // open: load, D, count
  D_Flip_Flop d_ff_2 (.clk(clock_1_out), .D(d_ff_1_q), .Q(d_ff_2_q), .reset(d_ff_3_q));  // open: Qn, preset, en
  D_Flip_Flop d_ff_3 (.clk(clock_1_out), .D(d_ff_2_q), .Q(d_ff_3_q), .reset(d_ff_3_q));  // open: Qn, preset, en
endmodule

module teste (
  input  in_1,
  output [7:0] Saida_Segundo
);

  Counter #(.max('h10), .ongoal("stay")) counter_1 (.Q(Saida_Segundo), .clk(in_1));  // open: load, D, count, carry, clr
endmodule
